// Logisim project lab08.circ as structural Verilog: 5 circuits, main circuit main
module main (
  input  [3:0] ALUOperation,
  input  [7:0] A,
  input  [7:0] B,
  output zero,
  output [7:0] out_5,
  output overflow
);

  _8_bit_ALU u_8_bit_alu_1 (
    .A(A), .B(B), .Ainvert(ALUOperation[3]), .Bnegate(ALUOperation[2]), .Operation(ALUOperation[1:0]),
    .zero(zero), .Result(out_5), .overflow(overflow));
endmodule

// ALU
module _1_bit_ALU (
  input  [1:0] Operation,
  input  Cin,
  input  Ainvert,
  input  Binvert,
  input  A,
  input  B,
  input  Less,
  output Result,
  output Cout
);

  wire adder_1_out, and_1_out, multiplexer_1_out, multiplexer_2_out, not_1_out, not_2_out, or_1_out;

  not not_1 (not_1_out, A);
  not not_2 (not_2_out, B);
  Multiplexer #(.enable("false")) multiplexer_1 (.in0(A), .in1(not_1_out), .out(multiplexer_1_out), .sel(Ainvert));
  Multiplexer #(.enable("false")) multiplexer_2 (.in0(B), .in1(not_2_out), .out(multiplexer_2_out), .sel(Binvert));
  and and_1 (and_1_out, multiplexer_1_out, multiplexer_2_out);
  or or_1 (or_1_out, multiplexer_1_out, multiplexer_2_out);
  Adder #(.width(1)) adder_1 (.a(multiplexer_1_out), .b(multiplexer_2_out), .out(adder_1_out), .cin(Cin), .cout(Cout));
  Multiplexer #(.select(2), .enable("false")) multiplexer_3 (
    .in0(and_1_out), .in1(or_1_out), .in2(adder_1_out), .in3(Less), .out(Result), .sel(Operation));

  // Notes on the sheet:
  //   Result: pull=up
endmodule

module _8_bit_ALU (
  input  Bnegate,
  input  [1:0] Operation,
  input  Ainvert,
  input  [7:0] A,
  input  [7:0] B,
  output zero,
  output [7:0] Result,
  output overflow
);

  wire n1_bit_alu_1_cout, n1_bit_alu_2_cout, n1_bit_alu_3_cout, n1_bit_alu_4_cout, n1_bit_alu_5_cout,
       n1_bit_alu_6_cout, n1_bit_alu_7_cout, or_1_out, xor_1_out;

  _1_bit_ALU u_1_bit_alu_1 (
    .A(A[0]), .B(B[0]), .Less(xor_1_out), .Ainvert(Ainvert), .Binvert(Bnegate), .Cin(Bnegate),
    .Operation(Operation), .Cout(n1_bit_alu_1_cout), .Result(Result[0]));
  _1_bit_ALU u_1_bit_alu_2 (
    .A(A[1]), .B(B[1]), .Less(1'b0), .Ainvert(Ainvert), .Binvert(Bnegate), .Cin(n1_bit_alu_1_cout),
    .Operation(Operation), .Cout(n1_bit_alu_2_cout), .Result(Result[1]));
  _1_bit_ALU u_1_bit_alu_3 (
    .A(A[2]), .B(B[2]), .Less(1'b0), .Ainvert(Ainvert), .Binvert(Bnegate), .Cin(n1_bit_alu_2_cout),
    .Operation(Operation), .Cout(n1_bit_alu_3_cout), .Result(Result[2]));
  _1_bit_ALU u_1_bit_alu_4 (
    .A(A[3]), .B(B[3]), .Less(1'b0), .Ainvert(Ainvert), .Binvert(Bnegate), .Cin(n1_bit_alu_3_cout),
    .Operation(Operation), .Cout(n1_bit_alu_4_cout), .Result(Result[3]));
  _1_bit_ALU u_1_bit_alu_5 (
    .A(A[4]), .B(B[4]), .Less(1'b0), .Ainvert(Ainvert), .Binvert(Bnegate), .Cin(n1_bit_alu_4_cout),
    .Operation(Operation), .Cout(n1_bit_alu_5_cout), .Result(Result[4]));
  _1_bit_ALU u_1_bit_alu_6 (
    .A(A[5]), .B(B[5]), .Less(1'b0), .Ainvert(Ainvert), .Binvert(Bnegate), .Cin(n1_bit_alu_5_cout),
    .Operation(Operation), .Cout(n1_bit_alu_6_cout), .Result(Result[5]));
  _1_bit_ALU u_1_bit_alu_7 (
    .A(A[6]), .B(B[6]), .Less(1'b0), .Ainvert(Ainvert), .Binvert(Bnegate), .Cin(n1_bit_alu_6_cout),
    .Operation(Operation), .Cout(n1_bit_alu_7_cout), .Result(Result[6]));
  _1_bit_ALU u_1_bit_alu_8 (
    .A(A[7]), .B(B[7]), .Less(1'b0), .Ainvert(Ainvert), .Binvert(Bnegate), .Cin(n1_bit_alu_7_cout),
    .Operation(Operation), .Result(Result[7]));  // open: Cout
  overflow overflow_1 (.A(Ainvert), .B(Bnegate), .Result(Result[7]), .Operation(Bnegate), .overflow(overflow));
  xor xor_1 (xor_1_out, Result[7], overflow);
  or or_1 (or_1_out, Result[0], Result[1], Result[2], Result[3], Result[4], Result[5], Result[6], Result[7]);
  not not_1 (zero, or_1_out);
endmodule

module overflow (
  input  A,
  input  Operation,
  input  B,
  input  Result,
  output overflow
);

  wire and_1_out, and_2_out, and_3_out, and_4_out, not_1_out, not_2_out, not_3_out, or_1_out, or_2_out;

  not not_1 (not_1_out, A);
  not not_2 (not_2_out, B);
  not not_3 (not_3_out, Result);
  and and_1 (and_1_out, A, B, not_3_out);
  and and_2 (and_2_out, not_1_out, not_2_out, Result);
  and and_3 (and_3_out, A, not_3_out, Result);
  and and_4 (and_4_out, not_1_out, B, not_3_out);
  or or_1 (or_1_out, and_1_out, and_2_out);
  or or_2 (or_2_out, and_3_out, and_4_out);
  Multiplexer #(.enable("false")) multiplexer_1 (.in0(or_1_out), .in1(or_2_out), .out(overflow), .sel(Operation));
endmodule

module overflow_2 (
  input  in_1,
  input  in_2,
  input  in_3,
  output out_4
);

  wire and_1_out, and_2_out, and_3_out, and_4_out, not_1_out, not_2_out, not_3_out, or_1_out, or_2_out;

  not not_1 (not_1_out, in_1);
  not not_2 (not_2_out, in_2);
  not not_3 (not_3_out, in_3);
  and and_1 (and_1_out, not_1_out, not_2_out, in_3);
  and and_2 (and_2_out, in_1, in_2, not_3_out);
  and and_3 (and_3_out, in_1, not_2_out, in_3);
  and and_4 (and_4_out, not_1_out, in_2, not_1_out);
  or or_1 (or_1_out, and_1_out, and_2_out);
  or or_2 (or_2_out, and_3_out, and_4_out);
  or or_3 (out_4, or_1_out, or_2_out);
endmodule
