// Logisim project Lab 09.circ as structural Verilog: 1 circuit, main circuit main
module main (
  input  [31:0] Input,
  input  Enable,
  input  [2:0] Select,
  input  [2:0] Select_2,
  input  [2:0] in_5,
  input  Clock,
  output [31:0] \output ,
  output [31:0] output_2
);

  wire and_1_out, and_2_out, and_3_out, and_4_out, and_5_out, and_6_out, and_7_out, and_8_out,
       decoder_1_out0, decoder_1_out1, decoder_1_out2, decoder_1_out3, decoder_1_out4, decoder_1_out5,
       decoder_1_out6, decoder_1_out7;
  wire [31:0] register_1_q, register_2_q, register_3_q, register_4_q, register_5_q, register_6_q,
       register_7_q, register_8_q;

  Decoder #(.select(3)) decoder_1 (
    .out0(decoder_1_out0), .out1(decoder_1_out1), .out2(decoder_1_out2), .out3(decoder_1_out3),
    .out4(decoder_1_out4), .out5(decoder_1_out5), .out6(decoder_1_out6), .out7(decoder_1_out7), .sel(in_5));  // open: en
  and and_1 (and_1_out, Enable, decoder_1_out0);
  and and_2 (and_2_out, Enable, decoder_1_out1);
  and and_3 (and_3_out, Enable, decoder_1_out2);
  and and_4 (and_4_out, Enable, decoder_1_out3);
  Register #(.width(32)) register_1 (.D(Input), .en(and_1_out), .Q(register_1_q), .clk(Clock), .clr(1'b0));
  Register #(.width(32)) register_2 (.D(Input), .en(and_2_out), .Q(register_2_q), .clk(Clock), .clr(1'b0));
  Register #(.width(32)) register_3 (.D(Input), .en(and_3_out), .Q(register_3_q), .clk(Clock), .clr(1'b0));
  Register #(.width(32)) register_4 (.D(Input), .en(and_4_out), .Q(register_4_q), .clk(Clock), .clr(1'b0));
  and and_5 (and_5_out, Enable, decoder_1_out4);
  and and_6 (and_6_out, Enable, decoder_1_out5);
  and and_7 (and_7_out, Enable, decoder_1_out6);
  and and_8 (and_8_out, Enable, decoder_1_out7);
  Register #(.width(32)) register_5 (.D(Input), .en(and_5_out), .Q(register_5_q), .clk(Clock), .clr(1'b0));
  Register #(.width(32)) register_6 (.D(Input), .en(and_6_out), .Q(register_6_q), .clk(Clock), .clr(1'b0));
  Register #(.width(32)) register_7 (.D(Input), .en(and_7_out), .Q(register_7_q), .clk(Clock), .clr(1'b0));
  Register #(.width(32)) register_8 (.D(Input), .en(and_8_out), .Q(register_8_q), .clk(Clock), .clr(1'b0));
  Multiplexer #(.select(3), .width(32)) multiplexer_1 (
    .in0(register_1_q), .in1(register_2_q), .in2(register_3_q), .in3(register_4_q), .in4(register_5_q),
    .in5(register_6_q), .in6(register_7_q), .in7(register_8_q), .out(\output ), .sel(Select));  // open: en
  Multiplexer #(.select(3), .width(32)) multiplexer_2 (
    .in0(register_1_q), .in1(register_2_q), .in2(register_3_q), .in3(register_4_q), .in4(register_5_q),
    .in5(register_6_q), .in6(register_7_q), .in7(register_8_q), .out(output_2), .sel(Select_2));  // open: en
endmodule
