// Logisim project Lab10.circ as structural Verilog: 1 circuit, main circuit main
module main (
  input  [7:0] Multiplier,
  input  [7:0] Multiplicand,
  input  Initialize,
  output [15:0] Output
);

  wire and_1_out, and_2_out, clock_1_out, Counter_carry, not_1_out, not_2_out, or_1_out;
  wire [3:0] Counter_q;
  wire [7:0] multiplexer_1_out, Multiplier_q, shifter_1_out;
  wire [15:0] multiplexer_2_out, multiplexer_3_out, multiplexer_4_out, Multiplicand_q, Product_q,
       shifter_2_out;

  Multiplexer #(.width(8), .enable("false")) multiplexer_1 (
    .in0(Multiplier), .in1(shifter_1_out), .out(multiplexer_1_out), .sel(or_1_out));
  Multiplexer #(.width(16), .enable("false")) multiplexer_2 (
    .in0({{8{1'b0}}, Multiplicand}), .in1(shifter_2_out), .out(multiplexer_2_out), .sel(or_1_out));
  Register #(.trigger("falling")) u_Multiplier (
    .D(multiplexer_1_out), .Q(Multiplier_q), .clk(and_2_out));  // open: en, clr
  Register #(.width(16), .trigger("falling")) u_Multiplicand (
    .D(multiplexer_2_out), .Q(Multiplicand_q), .clk(and_2_out));  // open: en, clr
  Shifter #(.shift("lr")) shifter_1 (.in(Multiplier_q), .\dist (3'b001), .out(shifter_1_out));
  Shifter #(.width(16)) shifter_2 (.in(Multiplicand_q), .\dist (4'b0001), .out(shifter_2_out));
  Multiplexer #(.width(16), .enable("false")) multiplexer_3 (
    .in0({16{1'b0}}), .in1(Output), .out(multiplexer_3_out), .sel(or_1_out));
  Clock clock_1 (.out(clock_1_out));
  Multiplexer #(.width(16), .enable("false")) multiplexer_4 (
    .in0({16{1'b0}}), .in1(Multiplicand_q), .out(multiplexer_4_out), .sel(Multiplier_q[0]));
  Register #(.width(16), .trigger("falling")) Product (
    .D(multiplexer_3_out), .Q(Product_q), .clk(and_2_out));  // open: en, clr
  not not_1 (not_1_out, Initialize);
  and and_1 (and_1_out, Initialize, clock_1_out);
  Adder #(.width(16)) adder_1 (.a(Product_q), .b(multiplexer_4_out), .out(Output));  // open: cin, cout
  Counter #(.width(4), .max('h9), .ongoal("stay"), .trigger("falling")) Counter (
    .Q(Counter_q), .carry(Counter_carry), .clk(and_1_out), .clr(not_1_out));  // open: load, D, count
  not not_2 (not_2_out, Counter_carry);
  or or_1 (or_1_out, Counter_q[0], Counter_q[1], Counter_q[2], Counter_q[3]);
  and and_2 (and_2_out, not_2_out, and_1_out);
endmodule
