// Logisim project project4_div_sqrt.circ as structural Verilog: 3 circuits, main circuit main
module main (
  input  [15:0] Divisor,
  input  [15:0] Dividend,
  input  Initialize,
  output [15:0] Quotient,
  output [31:0] Reminder
);

  wire and_1_out, and_2_out, Clock_out, comparator_1_eq, Counter_carry, not_1_out, not_2_out, not_3_out,
       not_4_out, or_1_out;
  wire [0:0] not_5_out;
  wire [7:0] Counter_q;
  wire [15:0] multiplexer_1_out, shifter_1_out;
  wire [31:0] adder_1_out, Divisor_q, multiplexer_2_out, multiplexer_3_out, multiplexer_4_out, shifter_2_out,
       subtractor_1_out;

  Clock Clock (.out(Clock_out));
  not not_1 (not_1_out, Initialize);
  and and_1 (and_1_out, Initialize, Clock_out);
  Counter #(.max('h12), .ongoal("stay"), .trigger("falling")) Counter (
    .Q(Counter_q), .carry(Counter_carry), .clk(and_1_out), .clr(not_1_out));  // open: load, D, count
  not not_2 (not_2_out, Counter_carry);
  or or_1 (or_1_out, Counter_q[0], Counter_q[1], Counter_q[2], Counter_q[3], Counter_q[4], Counter_q[5], Counter_q[6], Counter_q[7]);
  and and_2 (and_2_out, not_2_out, and_1_out);
  Multiplexer #(.width(16), .enable("false")) multiplexer_1 (
    .in0({16{1'b0}}), .in1({shifter_1_out[15:1], not_5_out[0]}), .out(multiplexer_1_out), .sel(or_1_out));
  Multiplexer #(.width(32), .enable("false")) multiplexer_2 (
    .in0({Divisor, {16{1'b0}}}), .in1(shifter_2_out), .out(multiplexer_2_out), .sel(or_1_out));
  Multiplexer #(.width(32), .enable("false")) multiplexer_3 (
    .in0({{16{1'b0}}, Dividend}), .in1(adder_1_out), .out(multiplexer_3_out), .sel(or_1_out));
  not not_3 (not_3_out, comparator_1_eq);
  Comparator #(.width(32)) comparator_1 (.a({32{1'b0}}), .b(multiplexer_2_out), .eq(comparator_1_eq));  // open: gt, lt
  not not_4 (not_4_out, comparator_1_eq);
  Register #(.width(16), .trigger("falling")) u_Quotient (
    .D(multiplexer_1_out), .en(not_3_out), .Q(Quotient), .clk(and_2_out));  // open: clr
  Register #(.width(32), .trigger("falling")) u_Divisor (
    .D(multiplexer_2_out), .Q(Divisor_q), .clk(and_2_out));  // open: en, clr
  Register #(.width(32), .trigger("falling")) u_Reminder (
    .D(multiplexer_3_out), .en(not_4_out), .Q(Reminder), .clk(and_2_out));  // open: clr
  Shifter #(.width(16)) shifter_1 (.in(Quotient), .\dist (4'b0001), .out(shifter_1_out));
  Shifter #(.width(32), .shift("lr")) shifter_2 (.in(Divisor_q), .\dist (5'b00001), .out(shifter_2_out));
  Subtractor #(.width(32)) subtractor_1 (.a(Reminder), .b(Divisor_q), .out(subtractor_1_out));  // open: bin, bout
  not not_5 (not_5_out[0], subtractor_1_out[31]);
  Multiplexer #(.width(32), .enable("false")) multiplexer_4 (
    .in0({32{1'b0}}), .in1(Divisor_q), .out(multiplexer_4_out), .sel(subtractor_1_out[31]));
  Adder #(.width(32)) adder_1 (.a(subtractor_1_out), .b(multiplexer_4_out), .out(adder_1_out));  // open: cin, cout
endmodule

module _8_bit_Square_Root (
  input  [7:0] Input,
  output [3:0] out_2
);

  wire [7:0] square_root_1_reminder, square_root_1_result, square_root_2_reminder, square_root_2_result,
       square_root_3_reminder, square_root_3_result;
  wire [7:4] square_root_4_result;

  Square_root square_root_1 (
    .CurrentResult({8{1'b0}}), .Current_Reminder({8{1'b0}}), .Current(Input[7:6]),
    .Result(square_root_1_result), .Reminder(square_root_1_reminder));
  Square_root square_root_2 (
    .CurrentResult(square_root_1_result), .Current_Reminder(square_root_1_reminder), .Current(Input[5:4]),
    .Result(square_root_2_result), .Reminder(square_root_2_reminder));
  Square_root square_root_3 (
    .CurrentResult(square_root_2_result), .Current_Reminder(square_root_2_reminder), .Current(Input[3:2]),
    .Result(square_root_3_result), .Reminder(square_root_3_reminder));
  Square_root square_root_4 (
    .CurrentResult(square_root_3_result), .Current_Reminder(square_root_3_reminder), .Current(Input[1:0]),
    .Result({square_root_4_result, out_2}));  // open: Reminder
endmodule

module Square_root (
  input  [7:0] CurrentResult,
  input  [7:0] Current_Reminder,
  input  [1:0] Current,
  output [7:0] Result,
  output [7:0] Reminder
);

  wire comparator_1_gt;
  wire [7:0] adder_1_out, adder_2_out, multiplexer_1_out, multiplexer_2_out, shifter_1_out, shifter_2_out,
       shifter_3_out;

  Shifter shifter_1 (.in(CurrentResult), .\dist (3'b001), .out(shifter_1_out));
  Shifter shifter_2 (.in(CurrentResult), .\dist (3'b010), .out(shifter_2_out));
  Shifter shifter_3 (.in(Current_Reminder), .\dist (3'b010), .out(shifter_3_out));
  Adder adder_1 (.a(shifter_2_out), .b(8'h1), .out(adder_1_out));  // open: cin, cout
  Adder adder_2 (.a(shifter_3_out), .b({{6{1'b0}}, Current}), .out(adder_2_out));  // open: cin, cout
  Multiplexer #(.width(8), .enable("false")) multiplexer_1 (
    .in0(8'h1), .in1({8{1'b0}}), .out(multiplexer_1_out), .sel(comparator_1_gt));
  Comparator comparator_1 (.a(adder_1_out), .b(adder_2_out), .gt(comparator_1_gt));  // open: eq, lt
  Multiplexer #(.width(8), .enable("false")) multiplexer_2 (
    .in0(adder_1_out), .in1({8{1'b0}}), .out(multiplexer_2_out), .sel(comparator_1_gt));
  Adder adder_3 (.a(shifter_1_out), .b(multiplexer_1_out), .out(Result));  // open: cin, cout
  Subtractor subtractor_1 (.a(adder_2_out), .b(multiplexer_2_out), .out(Reminder));  // open: bin, bout
endmodule
